// Logisim project cpu.circ as structural Verilog: 2 circuits, main circuit main
module main (
);

  wire dipswitch_1_sw5, dipswitch_1_sw6, dipswitch_1_sw7, dipswitch_1_sw8, dipswitch_1_sw9, dipswitch_1_sw10,
       dipswitch_1_sw11, dipswitch_1_sw12, dipswitch_1_sw13, dipswitch_1_sw14, dipswitch_1_sw15,
       dipswitch_1_sw16, ones_digit_1_p1, ones_digit_1_p3, ones_digit_1_p4, ones_digit_1_p5, undriven;

  _7_Segment_Display u_7_segment_display_1 ();  // open: g, f, a, b, e, d, c, dp
  // ones_digit ones_digit_1: pin names not known; wires that end beside it: ones_digit_1_p1, ones_digit_1_p1, ones_digit_1_p3, ones_digit_1_p4, ones_digit_1_p5
  DipSwitch #(.number(16)) dipswitch_1 (
    .sw1(ones_digit_1_p1), .sw2(ones_digit_1_p3), .sw3(ones_digit_1_p4), .sw4(ones_digit_1_p5),
    .sw5(dipswitch_1_sw5), .sw6(dipswitch_1_sw6), .sw7(dipswitch_1_sw7), .sw8(dipswitch_1_sw8),
    .sw9(dipswitch_1_sw9), .sw10(dipswitch_1_sw10), .sw11(dipswitch_1_sw11), .sw12(dipswitch_1_sw12),
    .sw13(dipswitch_1_sw13), .sw14(dipswitch_1_sw14), .sw15(dipswitch_1_sw15), .sw16(dipswitch_1_sw16));
  _7_Segment_Display u_7_segment_display_2 (.a(undriven));  // open: g, f, b, e, d, c, dp
endmodule

module ones_digit (
  input  _0,
  input  _1,
  input  _2,
  input  _3,
  input  _4,
  input  _5,
  input  _6,
  input  _7,
  input  _8,
  input  _9,
  input  _10,
  input  _11,
  input  _12,
  input  _13,
  input  _14,
  input  _15,
  output a,
  output b,
  output c,
  output d,
  output e,
  output f,
  output g
);

  wire or_1_out, or_2_out, or_3_out, or_4_out, or_5_out, or_6_out, or_7_out, or_8_out, or_9_out, or_10_out,
       or_11_out, or_13_out, or_15_out;

  or or_1 (or_1_out, _0, _5);
  or or_2 (or_2_out, _1, _6);
  or or_3 (or_3_out, _2, _7);
  or or_4 (or_4_out, _3, _8);
  or or_5 (or_5_out, _4, _9);
  or or_6 (or_6_out, _10, _15);
  or or_7 (or_7_out, or_2_out, _11);
  or or_8 (or_8_out, or_3_out, _12);
  or or_9 (or_9_out, or_4_out, _13);
  or or_10 (or_10_out, or_5_out, _14);
  or or_11 (or_11_out, or_1_out, or_6_out);
  or or_12 (e, or_8_out, or_11_out);
  or or_13 (or_13_out, or_9_out, or_10_out);
  or or_14 (a, or_9_out, e);
  or or_15 (or_15_out, or_13_out, or_11_out);
  or or_16 (f, or_10_out, or_11_out);
  or or_17 (g, or_13_out, or_8_out);
  or or_18 (c, or_7_out, or_15_out);

  assign b = 1'b1;
  assign d = a;
endmodule
